// Logisim project mips.circ as structural Verilog: 8 circuits, main circuit main
module main (
  input  clk,
  input  reset
);

  wire keyboard_1_avail, processador_en_mon, processador_en_ram, processador_en_tec, processador_rd_ram,
       processador_wr_ram;
  wire [6:0] keyboard_1_data;
  wire [25:0] processador_add_imed, processador_pc;
  wire [31:0] mem_programa_dout_rom, memoria_dados_dout_bus, processador_din_bus;

  memoria_dados memoria_dados (
    .ADD_IMED(processador_add_imed), .DIN_BUS(processador_din_bus), .WR_RAM(processador_wr_ram),
    .EN_RAM(processador_en_ram), .RD_RAM(processador_rd_ram), .CLEAR_RAM(reset), .clk(clk),
    .DOUT_BUS(memoria_dados_dout_bus));
  mem_programa mem_programa (.ADD_ROM(processador_pc), .DOUT_ROM(mem_programa_dout_rom));
  processador processador (
    .DOUT_ROM(mem_programa_dout_rom), .DOUT_BUS(memoria_dados_dout_bus), .DOUT_TEC(keyboard_1_data),
    .reset(reset), .clk(clk), .PC(processador_pc), .EN_RAM(processador_en_ram), .WR_RAM(processador_wr_ram),
    .RD_RAM(processador_rd_ram), .ADD_IMED(processador_add_imed), .EN_TEC(processador_en_tec),
    .DIN_BUS(processador_din_bus), .EN_MON(processador_en_mon));
  TTY tty_1 (.data(processador_din_bus[6:0]), .clk(clk), .we(processador_en_mon), .clr(reset));
  Keyboard keyboard_1 (
    .clk(clk), .re(processador_en_tec), .clr(reset), .avail(keyboard_1_avail), .data(keyboard_1_data));
endmodule

module caminho_dados (
  input  [31:0] DOUT_ROM,
  input  [6:0] DOUT_TEC,
  input  [31:0] DOUT_BUS,
  input  [1:0] SEL_OP1,
  input  clk,
  input  SEL_OP2,
  input  WR_ACC,
  input  reset,
  input  SEL_ULA,
  output [5:0] OP_CODE,
  output [25:0] ADD_IMED,
  output [31:0] DIN_BUS
);

  wire [31:0] bit_extender_1_out, bit_extender_2_out, multiplexer_1_out, multiplexer_2_out, ULA_ula_out;

  Register #(.width(32)) IR (.D(DOUT_ROM), .Q({OP_CODE, ADD_IMED}), .clk(clk), .clr(reset));  // open: en
  assign bit_extender_1_out = {{25{1'b0}}, DOUT_TEC};  // Bit_Extender bit_extender_1
  Multiplexer #(.width(32)) multiplexer_1 (
    .in0(DOUT_BUS), .in1(bit_extender_2_out), .out(multiplexer_1_out), .sel(SEL_OP2), .en(1'b1));
  assign bit_extender_2_out = {{6{1'b0}}, ADD_IMED};  // Bit_Extender bit_extender_2
  Multiplexer #(.select(2), .width(32)) multiplexer_2 (
    .in0(DOUT_BUS), .in1(bit_extender_1_out), .in2(bit_extender_2_out), .in3(ULA_ula_out),
    .out(multiplexer_2_out), .sel(SEL_OP1), .en(1'b1));
  Register #(.width(32)) ACC (.D(multiplexer_2_out), .en(WR_ACC), .Q(DIN_BUS), .clk(clk), .clr(reset));
  ULA ULA (.in_A_ULA(DIN_BUS), .in_B_ULA(multiplexer_1_out), .sel_ULA(SEL_ULA), .ULA_out(ULA_ula_out));
endmodule

module ULA (
  input  [31:0] in_A_ULA,
  input  [31:0] in_B_ULA,
  input  sel_ULA,
  output [31:0] ULA_out
);

  wire [31:0] adder_1_out, subtractor_1_out;

  Adder #(.width(32)) adder_1 (.a(in_A_ULA), .b(in_B_ULA), .out(adder_1_out));  // open: cin, cout
  Subtractor #(.width(32)) subtractor_1 (.a(in_A_ULA), .b(in_B_ULA), .out(subtractor_1_out));  // open: bin, bout
  Multiplexer #(.width(32), .enable("false")) multiplexer_1 (
    .in0(adder_1_out), .in1(subtractor_1_out), .out(ULA_out), .sel(sel_ULA));
endmodule

module memoria_dados (
  input  [25:0] ADD_IMED,
  input  [31:0] DIN_BUS,
  input  clk,
  input  WR_RAM,
  input  EN_RAM,
  input  RD_RAM,
  input  CLEAR_RAM,
  output [31:0] DOUT_BUS
);

  RAM #(.addrWidth(24), .dataWidth(32), .bus("separate")) ram_1 (
    .addr(ADD_IMED[23:0]), .din(DIN_BUS), .data(DOUT_BUS), .str(WR_RAM), .sel(EN_RAM), .clk(clk),
    .ld(RD_RAM), .clr(CLEAR_RAM));
endmodule

module logica_controle (
  input  [5:0] OP_CODE,
  output EN_RAM,
  output WR_RAM,
  output RD_RAM,
  output SEL_JMP,
  output EN_TEC,
  output WR_ACC,
  output EN_PC,
  output SEL_ULA,
  output [1:0] SEL_OP_1,
  output SEL_OP_2,
  output EN_MON
);

  wire and_1_out, and_2_out, and_3_out, and_4_out, and_6_out, and_7_out, and_10_out, and_11_out, and_12_out,
       and_13_out, and_14_out, and_15_out, and_16_out, and_17_out, and_18_out, and_20_out, not_1_out,
       not_2_out, not_3_out, not_4_out, not_5_out, not_6_out, not_7_out, not_8_out, not_9_out, not_10_out,
       not_11_out, not_12_out, not_13_out, not_14_out, not_15_out, not_16_out, not_17_out, not_18_out,
       not_19_out, not_20_out, not_21_out, not_22_out, not_23_out, not_24_out, not_25_out, not_26_out,
       not_27_out, not_28_out, not_29_out, not_30_out, not_31_out, not_32_out, not_33_out, not_34_out,
       not_35_out, not_36_out, not_37_out, not_38_out, not_39_out, not_40_out, not_41_out, not_42_out,
       not_43_out, not_44_out, not_45_out, not_46_out, not_47_out, not_48_out, not_49_out, not_50_out,
       not_51_out, not_52_out, not_53_out, not_54_out, not_55_out, not_56_out, not_57_out, not_58_out,
       not_59_out, not_60_out, not_61_out, not_62_out, not_63_out, or_6_out;

  not not_1 (not_1_out, OP_CODE[5]);
  not not_2 (not_2_out, OP_CODE[4]);
  not not_3 (not_3_out, OP_CODE[3]);
  not not_4 (not_4_out, OP_CODE[2]);
  not not_5 (not_5_out, OP_CODE[1]);
  not not_6 (not_6_out, OP_CODE[5]);
  not not_7 (not_7_out, OP_CODE[4]);
  not not_8 (not_8_out, OP_CODE[3]);
  not not_9 (not_9_out, OP_CODE[0]);
  not not_10 (not_10_out, OP_CODE[5]);
  not not_11 (not_11_out, OP_CODE[4]);
  not not_12 (not_12_out, OP_CODE[3]);
  not not_13 (not_13_out, OP_CODE[0]);
  not not_14 (not_14_out, OP_CODE[5]);
  not not_15 (not_15_out, OP_CODE[4]);
  not not_16 (not_16_out, OP_CODE[3]);
  not not_17 (not_17_out, OP_CODE[2]);
  not not_18 (not_18_out, OP_CODE[1]);
  not not_19 (not_19_out, OP_CODE[5]);
  not not_20 (not_20_out, OP_CODE[4]);
  not not_21 (not_21_out, OP_CODE[3]);
  not not_22 (not_22_out, OP_CODE[0]);
  not not_23 (not_23_out, OP_CODE[5]);
  not not_24 (not_24_out, OP_CODE[4]);
  not not_25 (not_25_out, OP_CODE[3]);
  not not_26 (not_26_out, OP_CODE[0]);
  not not_27 (not_27_out, OP_CODE[5]);
  not not_28 (not_28_out, OP_CODE[4]);
  not not_29 (not_29_out, OP_CODE[2]);
  not not_30 (not_30_out, OP_CODE[1]);
  not not_31 (not_31_out, OP_CODE[0]);
  not not_32 (not_32_out, OP_CODE[5]);
  not not_33 (not_33_out, OP_CODE[4]);
  not not_34 (not_34_out, OP_CODE[2]);
  not not_35 (not_35_out, OP_CODE[1]);
  and and_1 (and_1_out, OP_CODE[3], OP_CODE[0]);
  not not_36 (not_36_out, OP_CODE[5]);
  not not_37 (not_37_out, OP_CODE[4]);
  not not_38 (not_38_out, OP_CODE[3]);
  not not_39 (not_39_out, OP_CODE[5]);
  not not_40 (not_40_out, OP_CODE[4]);
  not not_41 (not_41_out, OP_CODE[3]);
  not not_42 (not_42_out, OP_CODE[5]);
  not not_43 (not_43_out, OP_CODE[4]);
  not not_44 (not_44_out, OP_CODE[3]);
  not not_45 (not_45_out, OP_CODE[5]);
  not not_46 (not_46_out, OP_CODE[4]);
  not not_47 (not_47_out, OP_CODE[2]);
  not not_48 (not_48_out, OP_CODE[1]);
  not not_49 (not_49_out, OP_CODE[5]);
  not not_50 (not_50_out, OP_CODE[4]);
  not not_51 (not_51_out, OP_CODE[3]);
  not not_52 (not_52_out, OP_CODE[2]);
  not not_53 (not_53_out, OP_CODE[0]);
  not not_54 (not_54_out, OP_CODE[2]);
  not not_55 (not_55_out, OP_CODE[1]);
  not not_56 (not_56_out, OP_CODE[5]);
  not not_57 (not_57_out, OP_CODE[4]);
  not not_58 (not_58_out, OP_CODE[2]);
  not not_59 (not_59_out, OP_CODE[0]);
  and and_2 (and_2_out, not_1_out, not_2_out, not_3_out, not_4_out, not_5_out, OP_CODE[0]);
  and and_3 (and_3_out, not_6_out, not_7_out, not_8_out, OP_CODE[2], not_9_out);
  and and_4 (and_4_out, not_10_out, not_11_out, not_12_out, OP_CODE[1], not_13_out);
  and and_5 (WR_RAM, not_14_out, not_15_out, not_16_out, not_17_out, not_18_out, OP_CODE[0]);
  and and_6 (and_6_out, not_19_out, not_20_out, not_21_out, OP_CODE[2], not_22_out);
  and and_7 (and_7_out, not_23_out, not_24_out, not_25_out, OP_CODE[1], not_26_out);
  and and_8 (SEL_JMP, not_27_out, not_28_out, OP_CODE[3], not_29_out, not_30_out, not_31_out);
  and and_9 (EN_TEC, not_32_out, not_33_out, OP_CODE[3], not_34_out, not_35_out, OP_CODE[0]);
  not not_60 (not_60_out, OP_CODE[3]);
  not not_61 (not_61_out, OP_CODE[5]);
  not not_62 (not_62_out, OP_CODE[4]);
  not not_63 (not_63_out, OP_CODE[3]);
  and and_10 (and_10_out, not_36_out, not_37_out, not_38_out, OP_CODE[2]);
  and and_11 (and_11_out, not_39_out, not_40_out, not_41_out, OP_CODE[1], OP_CODE[0]);
  and and_12 (and_12_out, not_42_out, not_43_out, not_44_out, OP_CODE[2]);
  and and_13 (and_13_out, not_45_out, not_46_out, OP_CODE[3], not_47_out, not_48_out, OP_CODE[0]);
  and and_14 (and_14_out, not_49_out, not_50_out, not_51_out);
  and and_15 (and_15_out, not_52_out, not_53_out);
  and and_16 (and_16_out, not_54_out, not_55_out);
  and and_17 (and_17_out, OP_CODE[2], OP_CODE[0]);
  and and_18 (and_18_out, OP_CODE[1], OP_CODE[0]);
  and and_19 (EN_MON, not_56_out, not_57_out, OP_CODE[3], not_58_out, OP_CODE[1], not_59_out);
  or or_1 (RD_RAM, and_6_out, and_7_out);
  and and_20 (and_20_out, OP_CODE[1], not_60_out);
  and and_21 (SEL_ULA, not_61_out, not_62_out, not_63_out, OP_CODE[2], OP_CODE[1]);
  or or_2 (SEL_OP_1[1], and_10_out, and_11_out);
  or or_3 (SEL_OP_1[0], and_12_out, and_13_out);
  or or_4 (EN_RAM, and_2_out, and_3_out, and_4_out);
  or or_5 (WR_ACC, OP_CODE[5], OP_CODE[4], and_1_out, OP_CODE[2], and_20_out);
  or or_6 (or_6_out, and_15_out, and_16_out, and_17_out, and_18_out);
  and and_22 (SEL_OP_2, and_14_out, or_6_out);

  assign EN_PC = 1'b1;
endmodule

module caminho_controle (
  input  clk,
  input  [25:0] ADD_IMED,
  input  reset_pc,
  input  [5:0] OP_CODE,
  output [25:0] PC,
  output EN_MON,
  output SEL_OP_2,
  output [1:0] SEL_OP_1,
  output SEL_ULA,
  output WR_ACC,
  output EN_TEC,
  output RD_RAM,
  output WR_RAM,
  output EN_RAM
);

  wire logica_controle_1_en_pc, logica_controle_1_sel_jmp;
  wire [25:0] adder_1_out, PC_q;

  logica_controle logica_controle_1 (
    .OP_CODE(OP_CODE), .EN_RAM(EN_RAM), .WR_RAM(WR_RAM), .RD_RAM(RD_RAM),
    .SEL_JMP(logica_controle_1_sel_jmp), .EN_TEC(EN_TEC), .WR_ACC(WR_ACC), .EN_PC(logica_controle_1_en_pc),
    .SEL_ULA(SEL_ULA), .SEL_OP_1(SEL_OP_1), .SEL_OP_2(SEL_OP_2), .EN_MON(EN_MON));
  Register #(.width(26)) u_PC (.D(adder_1_out), .en(logica_controle_1_en_pc), .Q(PC_q), .clk(clk), .clr(reset_pc));
  Multiplexer #(.width(26), .enable("false")) multiplexer_1 (
    .in0(PC_q), .in1(ADD_IMED), .out(PC), .sel(logica_controle_1_sel_jmp));
  Adder #(.width(26)) adder_1 (.a(PC), .b(26'h1), .out(adder_1_out));  // open: cin, cout
endmodule

module mem_programa (
  input  [25:0] ADD_ROM,
  output [31:0] DOUT_ROM
);

  ROM #(.addrWidth(24), .dataWidth(32)) rom_1 (.addr(ADD_ROM[23:0]), .data(DOUT_ROM), .sel(1'b1));

  // Notes on the sheet:
  //   contents of rom_1 (hex, n*v repeats v):
  //   24000000 28000000 14000001 20000001
endmodule

module processador (
  input  [31:0] DOUT_ROM,
  input  [31:0] DOUT_BUS,
  input  [6:0] DOUT_TEC,
  input  reset,
  input  clk,
  output [25:0] PC,
  output EN_RAM,
  output WR_RAM,
  output RD_RAM,
  output [25:0] ADD_IMED,
  output EN_TEC,
  output [31:0] DIN_BUS,
  output EN_MON
);

  wire caminho_controle_1_sel_op_2, caminho_controle_1_sel_ula, caminho_controle_1_wr_acc;
  wire [1:0] caminho_controle_1_sel_op_1;
  wire [5:0] caminho_dados_op_code;

  caminho_dados caminho_dados (
    .DOUT_ROM(DOUT_ROM), .OP_CODE(caminho_dados_op_code), .DOUT_TEC(DOUT_TEC), .DOUT_BUS(DOUT_BUS),
    .SEL_OP1(caminho_controle_1_sel_op_1), .clk(clk), .SEL_OP2(caminho_controle_1_sel_op_2),
    .WR_ACC(caminho_controle_1_wr_acc), .reset(reset), .SEL_ULA(caminho_controle_1_sel_ula),
    .ADD_IMED(ADD_IMED), .DIN_BUS(DIN_BUS));
  caminho_controle caminho_controle_1 (
    .clk(clk), .ADD_IMED(ADD_IMED), .reset_pc(reset), .EN_MON(EN_MON),
    .SEL_OP_2(caminho_controle_1_sel_op_2), .SEL_OP_1(caminho_controle_1_sel_op_1),
    .SEL_ULA(caminho_controle_1_sel_ula), .WR_ACC(caminho_controle_1_wr_acc), .EN_TEC(EN_TEC),
    .RD_RAM(RD_RAM), .WR_RAM(WR_RAM), .EN_RAM(EN_RAM), .PC(PC), .OP_CODE(caminho_dados_op_code));
endmodule
