// Logisim project lab_04.circ as structural Verilog: 7 circuits, main circuit main
module main (
  input  clk,
  input  reset
);

  wire caminho_controle_1_en_ram, caminho_controle_1_rd_ram, caminho_controle_1_sel_op_2,
       caminho_controle_1_sel_ula, caminho_controle_1_wr_acc, caminho_controle_1_wr_ram;
  wire [1:0] caminho_controle_1_sel_op_1;
  wire [5:0] caminho_dados_1_op_code;
  wire [25:0] caminho_controle_1_pc, caminho_dados_1_add_ram;
  wire [31:0] caminho_dados_1_din_ram, mem_programa_1_dout_rom, memoria_dados_1_dout_ram;

  // Probe on mem_programa_1_dout_rom
  // Probe on caminho_dados_1_din_ram
  caminho_dados caminho_dados_1 (
    .DOUT_ROM(mem_programa_1_dout_rom), .OP_CODE(caminho_dados_1_op_code),
    .DOUT_RAM(memoria_dados_1_dout_ram), .SEL_OP1(caminho_controle_1_sel_op_1), .clk(clk),
    .SEL_OP2(caminho_controle_1_sel_op_2), .WR_ACC(caminho_controle_1_wr_acc), .reset(reset),
    .SEL_ULA(caminho_controle_1_sel_ula), .ADD_RAM(caminho_dados_1_add_ram), .DIN_RAM(caminho_dados_1_din_ram));
  mem_programa mem_programa_1 (.PC(caminho_controle_1_pc), .DOUT_ROM(mem_programa_1_dout_rom));
  memoria_dados memoria_dados_1 (
    .ADD_RAM(caminho_dados_1_add_ram), .DIN_RAM(caminho_dados_1_din_ram), .WR_RAM(caminho_controle_1_wr_ram),
    .EN_RAM(caminho_controle_1_en_ram), .RD_RAM(caminho_controle_1_rd_ram), .CLEAR_RAM(reset), .clk(clk),
    .DOUT_RAM(memoria_dados_1_dout_ram));
  caminho_controle caminho_controle_1 (
    .OP_CODE(caminho_dados_1_op_code), .WR_ACC(caminho_controle_1_wr_acc), .clk(clk),
    .SEL_ULA(caminho_controle_1_sel_ula), .reset_pc(reset), .SEL_OP_1(caminho_controle_1_sel_op_1),
    .SEL_OP_2(caminho_controle_1_sel_op_2), .RD_RAM(caminho_controle_1_rd_ram), .PC(caminho_controle_1_pc),
    .WR_RAM(caminho_controle_1_wr_ram), .EN_RAM(caminho_controle_1_en_ram));
endmodule

module caminho_dados (
  input  [31:0] DOUT_ROM,
  input  [31:0] DOUT_RAM,
  input  [1:0] SEL_OP1,
  input  clk,
  input  SEL_OP2,
  input  WR_ACC,
  input  reset,
  input  SEL_ULA,
  output [5:0] OP_CODE,
  output [25:0] ADD_RAM,
  output [31:0] DIN_RAM
);

  wire [31:0] bit_extender_1_out, multiplexer_1_out, multiplexer_2_out, ULA_ula_out;

  Register #(.width(32)) IR (.D(DOUT_ROM), .Q({OP_CODE, ADD_RAM}), .clk(clk), .clr(reset));  // open: en
  Multiplexer #(.width(32)) multiplexer_1 (
    .in0(DOUT_RAM), .in1(bit_extender_1_out), .out(multiplexer_1_out), .sel(SEL_OP2), .en(1'b1));
  assign bit_extender_1_out = {{6{1'b0}}, ADD_RAM};  // Bit_Extender bit_extender_1
  Multiplexer #(.select(2), .width(32)) multiplexer_2 (
    .in0(DOUT_RAM), .in1(bit_extender_1_out), .in2(ULA_ula_out), .out(multiplexer_2_out), .sel(SEL_OP1),
    .en(1'b1));  // open: in3
  Register #(.width(32)) ACC (.D(multiplexer_2_out), .en(WR_ACC), .Q(DIN_RAM), .clk(clk), .clr(reset));
  ULA ULA (.in_A_ULA(DIN_RAM), .in_B_ULA(multiplexer_1_out), .sel_ULA(SEL_ULA), .ULA_out(ULA_ula_out));
endmodule

module ULA (
  input  [31:0] in_A_ULA,
  input  [31:0] in_B_ULA,
  input  sel_ULA,
  output [31:0] ULA_out
);

  wire [31:0] adder_1_out, subtractor_1_out;

  Adder #(.width(32)) adder_1 (.a(in_A_ULA), .b(in_B_ULA), .out(adder_1_out));  // open: cin, cout
  Subtractor #(.width(32)) subtractor_1 (.a(in_A_ULA), .b(in_B_ULA), .out(subtractor_1_out));  // open: bin, bout
  Multiplexer #(.width(32), .enable("false")) multiplexer_1 (
    .in0(adder_1_out), .in1(subtractor_1_out), .out(ULA_out), .sel(sel_ULA));
endmodule

module memoria_dados (
  input  [25:0] ADD_RAM,
  input  [31:0] DIN_RAM,
  input  clk,
  input  WR_RAM,
  input  EN_RAM,
  input  RD_RAM,
  input  CLEAR_RAM,
  output [31:0] DOUT_RAM
);

  RAM #(.addrWidth(24), .dataWidth(32), .bus("separate")) ram_1 (
    .addr(ADD_RAM[23:0]), .din(DIN_RAM), .data(DOUT_RAM), .str(WR_RAM), .sel(EN_RAM), .clk(clk), .ld(RD_RAM),
    .clr(CLEAR_RAM));
endmodule

module logica_controle (
  input  [5:0] OP_CODE,
  output EN_PC,
  output EN_RAM,
  output WR_ACC,
  output SEL_ULA,
  output WR_RAM,
  output [1:0] SEL_OP_1,
  output RD_RAM,
  output SEL_OP_2
);

  wire and_4_out, and_5_out, and_6_out, and_8_out, and_9_out, not_1_out, not_2_out, not_3_out, not_4_out,
       not_5_out, not_6_out, not_7_out, not_8_out, not_9_out, not_10_out, not_11_out, not_12_out, not_13_out,
       not_14_out, not_15_out, not_16_out, not_17_out, not_18_out, not_19_out, not_20_out, not_21_out,
       not_22_out, not_23_out, not_24_out, not_25_out, not_26_out, not_27_out, not_28_out, not_29_out,
       not_30_out, not_31_out, not_32_out, not_33_out, not_34_out, not_35_out, not_36_out, not_37_out;

  or or_1 (EN_PC, OP_CODE[5], OP_CODE[4], OP_CODE[3], OP_CODE[2], OP_CODE[1], OP_CODE[0]);
  or or_2 (WR_ACC, OP_CODE[5], OP_CODE[4], OP_CODE[3], OP_CODE[2], OP_CODE[1]);
  and and_1 (SEL_ULA, not_1_out, not_2_out, not_3_out, OP_CODE[2], OP_CODE[1]);
  and and_2 (SEL_OP_1[1], not_4_out, not_5_out, not_6_out, OP_CODE[2]);
  and and_3 (SEL_OP_1[0], not_7_out, not_8_out, not_9_out, not_10_out, OP_CODE[1], OP_CODE[0]);
  or or_3 (SEL_OP_2, OP_CODE[5], OP_CODE[4], OP_CODE[3], not_11_out, OP_CODE[0]);
  not not_1 (not_1_out, OP_CODE[5]);
  not not_2 (not_2_out, OP_CODE[4]);
  not not_3 (not_3_out, OP_CODE[3]);
  not not_4 (not_4_out, OP_CODE[5]);
  not not_5 (not_5_out, OP_CODE[4]);
  not not_6 (not_6_out, OP_CODE[3]);
  not not_7 (not_7_out, OP_CODE[5]);
  not not_8 (not_8_out, OP_CODE[4]);
  not not_9 (not_9_out, OP_CODE[3]);
  not not_10 (not_10_out, OP_CODE[2]);
  not not_11 (not_11_out, OP_CODE[2]);
  not not_12 (not_12_out, OP_CODE[5]);
  not not_13 (not_13_out, OP_CODE[4]);
  not not_14 (not_14_out, OP_CODE[3]);
  not not_15 (not_15_out, OP_CODE[2]);
  not not_16 (not_16_out, OP_CODE[1]);
  not not_17 (not_17_out, OP_CODE[5]);
  not not_18 (not_18_out, OP_CODE[4]);
  not not_19 (not_19_out, OP_CODE[3]);
  not not_20 (not_20_out, OP_CODE[0]);
  not not_21 (not_21_out, OP_CODE[5]);
  not not_22 (not_22_out, OP_CODE[4]);
  not not_23 (not_23_out, OP_CODE[3]);
  not not_24 (not_24_out, OP_CODE[0]);
  not not_25 (not_25_out, OP_CODE[5]);
  not not_26 (not_26_out, OP_CODE[4]);
  not not_27 (not_27_out, OP_CODE[3]);
  not not_28 (not_28_out, OP_CODE[2]);
  not not_29 (not_29_out, OP_CODE[1]);
  not not_30 (not_30_out, OP_CODE[5]);
  not not_31 (not_31_out, OP_CODE[4]);
  not not_32 (not_32_out, OP_CODE[3]);
  not not_33 (not_33_out, OP_CODE[0]);
  not not_34 (not_34_out, OP_CODE[5]);
  not not_35 (not_35_out, OP_CODE[4]);
  not not_36 (not_36_out, OP_CODE[3]);
  not not_37 (not_37_out, OP_CODE[0]);
  and and_4 (and_4_out, not_12_out, not_13_out, not_14_out, not_15_out, not_16_out, OP_CODE[0]);
  and and_5 (and_5_out, not_17_out, not_18_out, not_19_out, OP_CODE[2], not_20_out);
  and and_6 (and_6_out, not_21_out, not_22_out, not_23_out, OP_CODE[1], not_24_out);
  and and_7 (WR_RAM, not_25_out, not_26_out, not_27_out, not_28_out, not_29_out, OP_CODE[0]);
  and and_8 (and_8_out, not_30_out, not_31_out, not_32_out, OP_CODE[2], not_33_out);
  and and_9 (and_9_out, not_34_out, not_35_out, not_36_out, OP_CODE[1], not_37_out);
  or or_4 (RD_RAM, and_8_out, and_9_out);
  or or_5 (EN_RAM, and_4_out, and_5_out, and_6_out);
endmodule

module caminho_controle (
  input  [5:0] OP_CODE,
  input  clk,
  input  reset_pc,
  output WR_ACC,
  output SEL_ULA,
  output [1:0] SEL_OP_1,
  output SEL_OP_2,
  output RD_RAM,
  output [25:0] PC,
  output WR_RAM,
  output EN_RAM
);

  wire logica_controle_1_en_pc;
  wire [25:0] adder_1_out;

  logica_controle logica_controle_1 (
    .OP_CODE(OP_CODE), .EN_PC(logica_controle_1_en_pc), .WR_ACC(WR_ACC), .SEL_ULA(SEL_ULA),
    .SEL_OP_1(SEL_OP_1), .SEL_OP_2(SEL_OP_2), .EN_RAM(EN_RAM), .WR_RAM(WR_RAM), .RD_RAM(RD_RAM));
  Register #(.width(26)) u_PC (.D(adder_1_out), .en(logica_controle_1_en_pc), .Q(PC), .clk(clk), .clr(reset_pc));
  Adder #(.width(26)) adder_1 (.a(PC), .b(26'h1), .out(adder_1_out));  // open: cin, cout
endmodule

module mem_programa (
  input  [25:0] PC,
  output [31:0] DOUT_ROM
);

  ROM #(.addrWidth(24), .dataWidth(32)) rom_1 (.addr(PC[23:0]), .data(DOUT_ROM), .sel(1'b1));

  // Notes on the sheet:
  //   contents of rom_1 (hex, n*v repeats v):
  //   c000005 4000000 c000003 4000001 10000000 4000002 18000001 14000006 1c000003 4000004 8000002 18000004
endmodule
